# Fritzing sketch Bare_Conduct_Switch (saved by Fritzing 0.9.3b)
breadboards: 1

parts:
  S1 = Pushbutton [package="[SMD]"]
  S2 = Momentary Switch [package=ksa_sealed_tac_switch]
  S3 = Momentary Switch [package=ksa_sealed_tac_switch]
  S4 = Momentary Switch [package=ksa_sealed_tac_switch]
  S5 = Momentary Switch [package=ksa_sealed_tac_switch]
  S6 = Momentary Switch [package=ksa_sealed_tac_switch]
  Part1 = Bare Conductive Touch Board

nets:
  N1: S1.Pin_1, S1.Pin_2, S2.1, S3.1, S4.1, S5.1, S6.1, Part1.GND
  N2: S1.Pin_3, S1.Pin_4, Part1.A5
  N3: S2.3, Part1.A0
  N4: S3.3, Part1.A1
  N5: S4.3, Part1.A2
  N6: S5.3, Part1.A3
  N7: S6.3, Part1.A4
